// Logisim project computer.circ as structural Verilog
module main (
  input  TURN_ON,
  input  OFF
);

  wire cpu_1_clock_out, cpu_1_monitor_write, ON_KEY, RESET;
  wire [6:0] cpu_1_monitor_out, USB_KEY;

  cpu cpu_1 (
    .ENABLE(TURN_ON), .RESET(OFF), .KEYBOARD_IN(USB_KEY), .MONITOR_WRITE(cpu_1_monitor_write),
    .MONITOR_OUT(cpu_1_monitor_out), .KEYBOARD_WRITE(ON_KEY), .CLOCK_OUT(cpu_1_clock_out), .RESET_OUT(RESET));
  TTY #(.cols(60), .rows(20)) tty_1 (
    .data(cpu_1_monitor_out), .clk(cpu_1_clock_out), .we(cpu_1_monitor_write), .clr(RESET));
  Keyboard keyboard_1 (.clk(ON_KEY), .clr(RESET), .data(USB_KEY));  // open: re, avail

  // Notes on the sheet:
  //   TYPE HERE
endmodule

module cpu (
  input  ENABLE,
  input  RESET,
  input  [6:0] KEYBOARD_IN,
  output CLOCK_OUT,
  output RESET_OUT,
  output KEYBOARD_WRITE,
  output [6:0] MONITOR_OUT,
  output MONITOR_WRITE
);

  wire AMA_RESET, AMA_WRITE, and_1_out, clock_1_out, INSTRUCT_REG_WRITE, IO_SELECT_REG_WRITE, JUMP,
       MAR_0_WRITE, MAR_1_WRITE, MAR_2_WRITE, MAR_3_WRITE, MAR_READ, not_1_out, or_1_out, or_2_out, or_3_out,
       or_4_out, OUTPUT_HIGH_WRITE, OUTPUT_LOW_WRITE, PC_ENB, PC_OUT, RAM_READ, RAM_WRITE, READ_8_BIT_OUTPUT,
       READ_KEYBOARD, REGFILE_TO_BUS, REGFILE_WRITE, RMA_RESET, RMA_WRITE, STEP_RESET;
  wire [1:0] multiplexer_1_out;
  wire [3:0] alu_1_data_out, alu_1_flag_out, alu_memory_access_1_data_out, controlled_buffer_1_out,
       instruction_register_1_always_out, io_selection_register_1_always_out, multiplexer_2_out,
       pull_resistor_4_node, pull_resistor_8_node, pull_resistor_12_node, pull_resistor_16_node, ram_1_dout,
       register_file_1_data_out_a, register_file_1_data_out_b, register_file_1_flag_out,
       register_memory_access_1_data_out, step_counter_1_data_out;
  wire [7:7] io_register_1_data_out;
  wire [15:0] program_counter_1_always_out;

  Clock clock_1 (.out(clock_1_out));
  clk clk_1 (.CLOCK_IN(clock_1_out), .CLOCK_ENABLE(ENABLE), .CLOCK_OUT(CLOCK_OUT));  // open: MANUAL_TICK, HALT
  Hex_Digit_Display hex_digit_display_1 (.value(pull_resistor_4_node));  // open: dp
  LED led_1 (.in(pull_resistor_4_node[3]));
  LED led_2 (.in(pull_resistor_4_node[2]));
  LED led_3 (.in(pull_resistor_4_node[1]));
  LED led_4 (.in(pull_resistor_4_node[0]));
  Pull_Resistor pull_resistor_1 (.node(pull_resistor_4_node[3]));
  Pull_Resistor pull_resistor_2 (.node(pull_resistor_4_node[2]));
  Pull_Resistor pull_resistor_3 (.node(pull_resistor_4_node[1]));
  Pull_Resistor pull_resistor_4 (.node(pull_resistor_4_node[0]));
  LED led_5 (.in(pull_resistor_8_node[3]));
  LED led_6 (.in(pull_resistor_8_node[2]));
  Pull_Resistor pull_resistor_5 (.node(pull_resistor_8_node[3]));
  Pull_Resistor pull_resistor_6 (.node(pull_resistor_8_node[2]));
  Hex_Digit_Display hex_digit_display_2 (.value(pull_resistor_8_node));  // open: dp
  LED led_7 (.in(pull_resistor_8_node[1]));
  LED led_8 (.in(pull_resistor_8_node[0]));
  LED led_9 (.in(pull_resistor_12_node[3]));
  Pull_Resistor pull_resistor_7 (.node(pull_resistor_8_node[1]));
  Pull_Resistor pull_resistor_8 (.node(pull_resistor_8_node[0]));
  Pull_Resistor pull_resistor_9 (.node(pull_resistor_12_node[3]));
  Hex_Digit_Display hex_digit_display_3 (.value(pull_resistor_12_node));  // open: dp
  LED led_10 (.in(pull_resistor_12_node[2]));
  LED led_11 (.in(pull_resistor_12_node[1]));
  LED led_12 (.in(pull_resistor_12_node[0]));
  Pull_Resistor pull_resistor_10 (.node(pull_resistor_12_node[2]));
  Pull_Resistor pull_resistor_11 (.node(pull_resistor_12_node[1]));
  Pull_Resistor pull_resistor_12 (.node(pull_resistor_12_node[0]));
  Hex_Digit_Display hex_digit_display_4 (.value(pull_resistor_16_node));  // open: dp
  LED led_13 (.in(pull_resistor_16_node[3]));
  LED led_14 (.in(pull_resistor_16_node[2]));
  LED led_15 (.in(pull_resistor_16_node[1]));
  Pull_Resistor pull_resistor_13 (.node(pull_resistor_16_node[3]));
  Pull_Resistor pull_resistor_14 (.node(pull_resistor_16_node[2]));
  Pull_Resistor pull_resistor_15 (.node(pull_resistor_16_node[1]));
  LED led_16 (.in(pull_resistor_16_node[0]));
  LED led_17 (.in(program_counter_1_always_out[15]));
  Pull_Resistor pull_resistor_16 (.node(pull_resistor_16_node[0]));
  LED led_18 (.in(program_counter_1_always_out[14]));
  LED led_19 (.in(program_counter_1_always_out[13]));
  LED led_20 (.in(program_counter_1_always_out[12]));
  LED led_21 (.in(program_counter_1_always_out[11]));
  LED led_22 (.in(program_counter_1_always_out[10]));
  LED led_23 (.in(program_counter_1_always_out[9]));
  LED led_24 (.in(program_counter_1_always_out[8]));
  LED led_25 (.in(program_counter_1_always_out[7]));
  io_selection_register io_selection_register_1 (
    .DATA_IN(controlled_buffer_1_out), .WRITE(IO_SELECT_REG_WRITE), .CLOCK(CLOCK_OUT), .RESET(RESET),
    .ALWAYS_OUT(io_selection_register_1_always_out));  // open: READ, DATA_OUT
  LED led_26 (.in(program_counter_1_always_out[4]));
  LED led_27 (.in(program_counter_1_always_out[3]));
  LED led_28 (.in(program_counter_1_always_out[6]));
  LED led_29 (.in(program_counter_1_always_out[5]));
  RAM #(.addrWidth(16), .dataWidth(4), .enables("line")) ram_1 (
    .addr({pull_resistor_4_node, pull_resistor_8_node, pull_resistor_12_node, pull_resistor_16_node}),
    .we(RAM_WRITE), .clk(CLOCK_OUT), .din(controlled_buffer_1_out), .dout(ram_1_dout));
  Demultiplexer #(.select(4)) demultiplexer_1 (
    .out1(MONITOR_WRITE), .in(READ_8_BIT_OUTPUT), .sel(io_selection_register_1_always_out));  // open: out0, out2, out3, out4, out5, out6, out7, out8, out9, out10, out11, out12, out13, out14, out15
  LED led_30 (.in(program_counter_1_always_out[2]));
  LED led_31 (.in(program_counter_1_always_out[1]));
  LED led_32 (.in(program_counter_1_always_out[0]));
  program_counter program_counter_1 (
    .COUNTER_OUT(PC_OUT), .RESET(RESET), .JUMP(JUMP), .COUNTER_ENABLE(PC_ENB), .CLOCK(CLOCK_OUT),
    .ADDRESS_IN({pull_resistor_4_node, pull_resistor_8_node, pull_resistor_12_node, pull_resistor_16_node}),
    .ALWAYS_OUT(program_counter_1_always_out),
    .ADDRESS_OUT({pull_resistor_4_node, pull_resistor_8_node, pull_resistor_12_node, pull_resistor_16_node}));
  memory_address_register memory_address_register_1 (
    .DATA_IN(controlled_buffer_1_out), .MAR_WRITE({MAR_3_WRITE, MAR_2_WRITE, MAR_1_WRITE, MAR_0_WRITE}),
    .CLOCK(CLOCK_OUT), .RESET(RESET), .MAR_OUT(MAR_READ),
    .DATA_OUT({pull_resistor_4_node, pull_resistor_8_node, pull_resistor_12_node, pull_resistor_16_node}));
  io_register io_register_1 (
    .READ(READ_8_BIT_OUTPUT), .CLOCK(CLOCK_OUT), .RESET(RESET), .WRITE_LOW(OUTPUT_LOW_WRITE),
    .WRITE_HIGH(OUTPUT_HIGH_WRITE), .DATA_IN(controlled_buffer_1_out),
    .DATA_OUT({io_register_1_data_out[7], MONITOR_OUT}));  // open: ALWAYS_OUT
  assign controlled_buffer_1_out = RAM_READ ? ram_1_dout : 4'bz;  // Controlled_Buffer controlled_buffer_1
  LED led_33 (.in(controlled_buffer_1_out[3]));
  LED led_34 (.in(controlled_buffer_1_out[2]));
  LED led_35 (.in(controlled_buffer_1_out[1]));
  Pull_Resistor pull_resistor_17 (.node(controlled_buffer_1_out[3]));
  Pull_Resistor pull_resistor_18 (.node(controlled_buffer_1_out[2]));
  Pull_Resistor pull_resistor_19 (.node(controlled_buffer_1_out[1]));
  LED led_36 (.in(io_register_1_data_out[7]));
  Pull_Resistor pull_resistor_20 (.node(io_register_1_data_out[7]));
  LED led_37 (.in(controlled_buffer_1_out[0]));
  Pull_Resistor pull_resistor_21 (.node(controlled_buffer_1_out[0]));
  Hex_Digit_Display hex_digit_display_5 (.value({io_register_1_data_out[7], MONITOR_OUT[6:4]}));  // open: dp
  LED led_38 (.in(MONITOR_OUT[6]));
  LED led_39 (.in(MONITOR_OUT[5]));
  LED led_40 (.in(MONITOR_OUT[4]));
  Pull_Resistor pull_resistor_22 (.node(MONITOR_OUT[6]));
  Pull_Resistor pull_resistor_23 (.node(MONITOR_OUT[5]));
  Pull_Resistor pull_resistor_24 (.node(MONITOR_OUT[4]));
  or or_1 (or_1_out, RESET, RMA_RESET);
  or or_2 (or_2_out, RESET, AMA_RESET);
  Hex_Digit_Display hex_digit_display_6 (.value(MONITOR_OUT[3:0]));  // open: dp
  LED led_41 (.in(MONITOR_OUT[3]));
  LED led_42 (.in(MONITOR_OUT[2]));
  LED led_43 (.in(MONITOR_OUT[1]));
  LED led_44 (.in(MONITOR_OUT[0]));
  Pull_Resistor pull_resistor_25 (.node(MONITOR_OUT[3]));
  Pull_Resistor pull_resistor_26 (.node(MONITOR_OUT[2]));
  Pull_Resistor pull_resistor_27 (.node(MONITOR_OUT[1]));
  Pull_Resistor pull_resistor_28 (.node(MONITOR_OUT[0]));
  register_memory_access register_memory_access_1 (
    .DATA_IN(controlled_buffer_1_out), .WRITE(RMA_WRITE), .CLOCK(CLOCK_OUT), .RESET(or_1_out),
    .DATA_OUT(register_memory_access_1_data_out));
  alu_memory_access alu_memory_access_1 (
    .DATA_IN(controlled_buffer_1_out), .WRITE(AMA_WRITE), .CLOCK(CLOCK_OUT), .RESET(or_2_out),
    .DATA_OUT(alu_memory_access_1_data_out));
  instruction_register instruction_register_1 (
    .DATA_IN(controlled_buffer_1_out), .WRITE(INSTRUCT_REG_WRITE), .CLOCK(CLOCK_OUT), .RESET(RESET),
    .ALWAYS_OUT(instruction_register_1_always_out));  // open: READ, DATA_OUT
  or or_3 (or_3_out, STEP_RESET, RESET);
  not not_1 (not_1_out, CLOCK_OUT);
  and and_1 (and_1_out, not_1_out, 1'b1);
  or or_4 (or_4_out, alu_memory_access_1_data_out[3], alu_memory_access_1_data_out[2]);
  assign controlled_buffer_1_out = REGFILE_TO_BUS ? register_file_1_data_out_b : 4'bz;  // Controlled_Buffer controlled_buffer_2
  Multiplexer #(.width(2)) multiplexer_1 (
    .in0(register_memory_access_1_data_out[3:2]), .in1(alu_memory_access_1_data_out[1:0]),
    .out(multiplexer_1_out), .sel(or_4_out));
  step_counter step_counter_1 (.RESET(or_3_out), .CLOCK(and_1_out), .DATA_OUT(step_counter_1_data_out));
  assign controlled_buffer_1_out = READ_KEYBOARD ? KEYBOARD_IN[3:0] : 4'bz;  // Controlled_Buffer controlled_buffer_3
  Hex_Digit_Display hex_digit_display_7 (.value(step_counter_1_data_out));  // open: dp
  alu alu_1 (
    .ENABLE(or_4_out), .SELECT_OP(alu_memory_access_1_data_out[3:2]), .A_IN(register_file_1_data_out_a),
    .B_IN(register_file_1_data_out_b), .DATA_OUT(alu_1_data_out), .FLAG_OUT(alu_1_flag_out));  // open: BORROW_IN, CARRY_IN, BORROW_OUT
  Multiplexer #(.width(4)) multiplexer_2 (
    .in0(controlled_buffer_1_out), .in1(alu_1_data_out), .out(multiplexer_2_out), .sel(or_4_out));
  control_unit control_unit_1 (
    .FLAG_IN(register_file_1_flag_out), .FROM_RAM(controlled_buffer_1_out),
    .INSTRUCTION(instruction_register_1_always_out), .STEP_COUNTER(step_counter_1_data_out),
    .CLOCK(CLOCK_OUT), .STEP_COUNTER_RESET(STEP_RESET), .RMA_RESET(RMA_RESET), .AMA_RESET(AMA_RESET),
    .MAR_WRITE({MAR_3_WRITE, MAR_2_WRITE, MAR_1_WRITE, MAR_0_WRITE}), .RAM_READ(RAM_READ),
    .REGFILE_READ(REGFILE_TO_BUS), .MAR_READ(MAR_READ), .IO_READ(READ_8_BIT_OUTPUT),
    .KEYBOARD_READ(READ_KEYBOARD), .INSTRUCTION_REG_WRITE(INSTRUCT_REG_WRITE), .RMA_WRITE(RMA_WRITE),
    .AMA_WRITE(AMA_WRITE), .REGFILE_WRITE(REGFILE_WRITE), .RAM_WRITE(RAM_WRITE),
    .IO_WRITE(IO_SELECT_REG_WRITE), .KEYBOARD_WRITE(KEYBOARD_WRITE), .NIBLE_HIGH_WRITE(OUTPUT_HIGH_WRITE),
    .NIBLE_LOW_WRITE(OUTPUT_LOW_WRITE), .PC_ENABLE(PC_ENB), .PC_OUT_DISABLE(PC_OUT), .JUMP_ENABLE(JUMP));
  register_file register_file_1 (
    .FLAG_CHECK(or_4_out), .CLOCK(CLOCK_OUT), .RESET(RESET), .WRITE_ENABLE(REGFILE_WRITE),
    .FLAG_IN(alu_1_flag_out), .WRITE(multiplexer_1_out), .SELECT_A(register_memory_access_1_data_out[3:2]),
    .SELECT_B(register_memory_access_1_data_out[1:0]), .DATA_IN(multiplexer_2_out),
    .DATA_OUT_A(register_file_1_data_out_a), .DATA_OUT_B(register_file_1_data_out_b),
    .FLAG_OUT(register_file_1_flag_out));

  assign RESET_OUT = RESET;

  // Notes on the sheet:
  //   ADDRESS BUS
  //   DATA BUS
endmodule

module clk (
  input  CLOCK_IN,
  input  CLOCK_ENABLE,
  input  MANUAL_TICK,
  input  HALT,
  output CLOCK_OUT
);

  wire and_1_out, and_2_out, not_1_out, not_2_out, or_1_out;

  not not_1 (not_1_out, CLOCK_ENABLE);
  and and_1 (and_1_out, CLOCK_IN, CLOCK_ENABLE);
  and and_2 (and_2_out, not_1_out, MANUAL_TICK);
  or or_1 (or_1_out, and_1_out, and_2_out);
  not not_2 (not_2_out, HALT);
  and and_3 (CLOCK_OUT, or_1_out, not_2_out);
endmodule

module program_counter (
  input  RESET,
  input  JUMP,
  input  COUNTER_ENABLE,
  input  CLOCK,
  input  [15:0] ADDRESS_IN,
  input  COUNTER_OUT,
  output [15:0] ALWAYS_OUT,
  output [15:0] ADDRESS_OUT
);

  wire not_1_out;

  not not_1 (not_1_out, COUNTER_OUT);
  Counter #(.max('hffff), .width(16)) counter_1 (
    .clr(RESET), .load(JUMP), .up(COUNTER_ENABLE), .count(COUNTER_ENABLE), .clk(CLOCK), .D(ADDRESS_IN),
    .Q(ALWAYS_OUT));  // open: carry
  assign ADDRESS_OUT = not_1_out ? ALWAYS_OUT : 16'bz;  // Controlled_Buffer controlled_buffer_1
endmodule

module memory_address_register (
  input  [3:0] DATA_IN,
  input  [3:0] MAR_WRITE,
  input  CLOCK,
  input  RESET,
  input  MAR_OUT,
  output [15:0] DATA_OUT
);

  wire [3:0] register_1_q, register_2_q, register_3_q, register_4_q;

  Register #(.width(4)) register_1 (.D(DATA_IN), .en(MAR_WRITE[0]), .clk(CLOCK), .Q(register_1_q), .clr(RESET));
  Register #(.width(4)) register_2 (.D(DATA_IN), .en(MAR_WRITE[1]), .clk(CLOCK), .Q(register_2_q), .clr(RESET));
  Register #(.width(4)) register_3 (.D(DATA_IN), .en(MAR_WRITE[2]), .clk(CLOCK), .Q(register_3_q), .clr(RESET));
  Register #(.width(4)) register_4 (.D(DATA_IN), .en(MAR_WRITE[3]), .clk(CLOCK), .Q(register_4_q), .clr(RESET));
  assign DATA_OUT[3:0] = MAR_OUT ? register_1_q : 4'bz;  // Controlled_Buffer controlled_buffer_1
  assign DATA_OUT[7:4] = MAR_OUT ? register_2_q : 4'bz;  // Controlled_Buffer controlled_buffer_2
  assign DATA_OUT[11:8] = MAR_OUT ? register_3_q : 4'bz;  // Controlled_Buffer controlled_buffer_3
  assign DATA_OUT[15:12] = MAR_OUT ? register_4_q : 4'bz;  // Controlled_Buffer controlled_buffer_4
endmodule

module alu (
  input  BORROW_IN,
  input  CARRY_IN,
  input  [3:0] A_IN,
  input  [3:0] B_IN,
  input  ENABLE,
  input  [1:0] SELECT_OP,
  output [3:0] DATA_OUT,
  output BORROW_OUT,
  output [3:0] FLAG_OUT
);

  wire [3:0] adder_1_out, subtractor_1_out;

  Adder #(.width(4)) adder_1 (.a(A_IN), .b(B_IN), .out(adder_1_out), .cin(CARRY_IN), .cout(FLAG_OUT[0]));
  Subtractor #(.width(4)) subtractor_1 (.a(A_IN), .b(B_IN), .out(subtractor_1_out), .bin(BORROW_IN), .bout(BORROW_OUT));
  Comparator #(.width(4)) comparator_1 (.a(A_IN), .b(B_IN), .gt(FLAG_OUT[1]), .eq(FLAG_OUT[2]), .lt(FLAG_OUT[3]));
  Multiplexer #(.enable("true"), .select(2), .width(4)) multiplexer_1 (
    .in1(adder_1_out), .in2(subtractor_1_out), .in3(FLAG_OUT), .out(DATA_OUT), .sel(SELECT_OP), .en(ENABLE));  // open: in0
endmodule

module register_file (
  input  [3:0] DATA_IN,
  input  [1:0] WRITE,
  input  WRITE_ENABLE,
  input  [1:0] SELECT_A,
  input  [1:0] SELECT_B,
  input  [3:0] FLAG_IN,
  input  FLAG_CHECK,
  input  CLOCK,
  input  RESET,
  output [3:0] DATA_OUT_A,
  output [3:0] DATA_OUT_B,
  output [3:0] FLAG_OUT
);

  wire and_1_out, decoder_1_out0, decoder_1_out1, decoder_1_out2, decoder_1_out3;
  wire [3:0] multiplexer_1_out, register_1_q, register_2_q, register_3_q;

  Decoder #(.select(2)) decoder_1 (
    .out0(decoder_1_out0), .out1(decoder_1_out1), .out2(decoder_1_out2), .out3(decoder_1_out3), .sel(WRITE),
    .en(WRITE_ENABLE));
  and and_1 (and_1_out, decoder_1_out3, FLAG_CHECK);
  Multiplexer #(.width(4)) multiplexer_1 (.in0(DATA_IN), .in1(FLAG_IN), .out(multiplexer_1_out), .sel(FLAG_CHECK));
  Register #(.width(4)) register_1 (.D(DATA_IN), .en(decoder_1_out0), .clk(CLOCK), .Q(register_1_q), .clr(RESET));
  Register #(.width(4)) register_2 (.D(DATA_IN), .en(decoder_1_out1), .clk(CLOCK), .Q(register_2_q), .clr(RESET));
  Register #(.width(4)) register_3 (.D(DATA_IN), .en(decoder_1_out2), .clk(CLOCK), .Q(register_3_q), .clr(RESET));
  Register #(.width(4)) register_4 (.D(multiplexer_1_out), .en(and_1_out), .clk(CLOCK), .Q(FLAG_OUT), .clr(RESET));
  Multiplexer #(.select(2), .width(4)) multiplexer_2 (
    .in0(register_1_q), .in1(register_2_q), .in2(register_3_q), .in3(FLAG_OUT), .out(DATA_OUT_A),
    .sel(SELECT_A));
  Multiplexer #(.select(2), .width(4)) multiplexer_3 (
    .in0(register_1_q), .in1(register_2_q), .in2(register_3_q), .in3(FLAG_OUT), .out(DATA_OUT_B),
    .sel(SELECT_B));

  // Notes on the sheet:
  //   FLAGS
endmodule

module register_memory_access (
  input  [3:0] DATA_IN,
  input  WRITE,
  input  CLOCK,
  input  RESET,
  output [3:0] DATA_OUT
);

  Register #(.width(4)) register_1 (.D(DATA_IN), .en(WRITE), .clk(CLOCK), .Q(DATA_OUT), .clr(RESET));
endmodule

module alu_memory_access (
  input  [3:0] DATA_IN,
  input  WRITE,
  input  CLOCK,
  input  RESET,
  output [3:0] DATA_OUT
);

  Register #(.width(4)) register_1 (.D(DATA_IN), .en(WRITE), .clk(CLOCK), .Q(DATA_OUT), .clr(RESET));
endmodule

module instruction_register (
  input  [3:0] DATA_IN,
  input  WRITE,
  input  CLOCK,
  input  RESET,
  input  READ,
  output [3:0] ALWAYS_OUT,
  output [3:0] DATA_OUT
);

  Register #(.width(4)) register_1 (.D(DATA_IN), .en(WRITE), .clk(CLOCK), .Q(ALWAYS_OUT), .clr(RESET));
  assign DATA_OUT = READ ? ALWAYS_OUT : 4'bz;  // Controlled_Buffer controlled_buffer_1
endmodule

module control_unit (
  input  [3:0] FLAG_IN,
  input  [3:0] FROM_RAM,
  input  CLOCK,
  input  [3:0] INSTRUCTION,
  input  [3:0] STEP_COUNTER,
  output JUMP_ENABLE,
  output RAM_READ,
  output REGFILE_READ,
  output MAR_READ,
  output IO_READ,
  output KEYBOARD_READ,
  output INSTRUCTION_REG_WRITE,
  output RMA_WRITE,
  output AMA_WRITE,
  output REGFILE_WRITE,
  output RAM_WRITE,
  output IO_WRITE,
  output STEP_COUNTER_RESET,
  output KEYBOARD_WRITE,
  output RMA_RESET,
  output NIBLE_HIGH_WRITE,
  output AMA_RESET,
  output NIBLE_LOW_WRITE,
  output PC_ENABLE,
  output PC_OUT_DISABLE,
  output [3:0] MAR_WRITE
);

  wire and_2_out, and_3_out, and_4_out, and_5_out, and_6_out, and_7_out, and_8_out, and_9_out,
       CONDITION_CHECK_STORE, decoder_1_out0, decoder_1_out1, decoder_1_out2, decoder_1_out3,
       micro_cycle_1_jump_enable, not_1_out, not_2_out, not_3_out, not_4_out, not_5_out, or_1_out;
  wire [3:0] register_1_q;

  and and_1 (CONDITION_CHECK_STORE, and_2_out, and_3_out);
  Register #(.width(4)) register_1 (
    .D(FROM_RAM), .en(CONDITION_CHECK_STORE), .clk(CLOCK), .Q(register_1_q), .clr(AMA_RESET));
  and and_2 (and_2_out, INSTRUCTION[0], INSTRUCTION[1], INSTRUCTION[2], not_1_out);
  not not_1 (not_1_out, INSTRUCTION[3]);
  not not_2 (not_2_out, STEP_COUNTER[0]);
  not not_3 (not_3_out, STEP_COUNTER[2]);
  and and_3 (and_3_out, not_2_out, STEP_COUNTER[1], not_3_out, not_4_out);
  not not_4 (not_4_out, STEP_COUNTER[3]);
  Decoder #(.disabled("Z"), .select(2)) decoder_1 (
    .out0(decoder_1_out0), .out1(decoder_1_out1), .out2(decoder_1_out2), .out3(decoder_1_out3),
    .sel(register_1_q[1:0]));  // open: en
  not not_5 (not_5_out, INSTRUCTION[3]);
  and and_4 (and_4_out, INSTRUCTION[0], INSTRUCTION[1], INSTRUCTION[2], not_5_out);
  and and_5 (and_5_out, FLAG_IN[0], decoder_1_out0);
  and and_6 (and_6_out, FLAG_IN[1], decoder_1_out1);
  and and_7 (and_7_out, FLAG_IN[2], decoder_1_out2);
  and and_8 (and_8_out, FLAG_IN[3], decoder_1_out3);
  micro_cycle micro_cycle_1 (
    .INSTRUCTION(INSTRUCTION), .STEP(STEP_COUNTER), .RAM_READ(RAM_READ), .REGFILE_READ(REGFILE_READ),
    .MAR_READ(MAR_READ), .IO_READ(IO_READ), .KEYBOARD_READ(KEYBOARD_READ),
    .INSTRUCTION_REG_WRITE(INSTRUCTION_REG_WRITE), .RMA_WRITE(RMA_WRITE), .AMA_WRITE(AMA_WRITE),
    .REGFILE_WRITE(REGFILE_WRITE), .RAM_WRITE(RAM_WRITE), .MAR_WRITE(MAR_WRITE), .IO_WRITE(IO_WRITE),
    .KEYBOARD_WRITE(KEYBOARD_WRITE), .NIBLE_HIGH_WRITE(NIBLE_HIGH_WRITE), .NIBLE_LOW_WRITE(NIBLE_LOW_WRITE),
    .PC_ENABLE(PC_ENABLE), .PC_OUT_DISABLE(PC_OUT_DISABLE), .JUMP_ENABLE(micro_cycle_1_jump_enable),
    .RMA_RESET(RMA_RESET), .AMA_RESET(AMA_RESET), .STEP_RESET(STEP_COUNTER_RESET));
  or or_1 (or_1_out, and_5_out, and_6_out, and_7_out, and_8_out);
  and and_9 (and_9_out, or_1_out, micro_cycle_1_jump_enable);
  Multiplexer multiplexer_1 (.in0(micro_cycle_1_jump_enable), .in1(and_9_out), .out(JUMP_ENABLE), .sel(and_4_out));

  // Other names for the same wires on the sheet: CONDITION_CHECK_RESET = AMA_RESET
endmodule

module step_counter (
  input  RESET,
  input  CLOCK,
  output [3:0] DATA_OUT
);

  Counter #(.max('hf), .width(4)) counter_1 (
    .clr(RESET), .up(1'b1), .count(1'b1), .clk(CLOCK), .Q(DATA_OUT));  // open: load, D, carry
endmodule

module io_selection_register (
  input  [3:0] DATA_IN,
  input  WRITE,
  input  READ,
  input  CLOCK,
  input  RESET,
  output [3:0] ALWAYS_OUT,
  output [3:0] DATA_OUT
);

  Register #(.width(4)) register_1 (.D(DATA_IN), .en(WRITE), .clk(CLOCK), .Q(ALWAYS_OUT), .clr(RESET));
  assign DATA_OUT = READ ? ALWAYS_OUT : 4'bz;  // Controlled_Buffer controlled_buffer_1
endmodule

module io_register (
  input  [3:0] DATA_IN,
  input  WRITE_LOW,
  input  WRITE_HIGH,
  input  READ,
  input  CLOCK,
  input  RESET,
  output [7:0] ALWAYS_OUT,
  output [7:0] DATA_OUT
);

  Register #(.width(4)) register_1 (.D(DATA_IN), .en(WRITE_LOW), .clk(CLOCK), .Q(ALWAYS_OUT[3:0]), .clr(RESET));
  Register #(.width(4)) register_2 (.D(DATA_IN), .en(WRITE_HIGH), .clk(CLOCK), .Q(ALWAYS_OUT[7:4]), .clr(RESET));
  assign DATA_OUT = READ ? ALWAYS_OUT : 8'bz;  // Controlled_Buffer controlled_buffer_1
endmodule

module micro_cycle (
  input  [3:0] INSTRUCTION,
  input  [3:0] STEP,
  output RAM_READ,
  output REGFILE_READ,
  output MAR_READ,
  output IO_READ,
  output KEYBOARD_READ,
  output INSTRUCTION_REG_WRITE,
  output RMA_WRITE,
  output AMA_WRITE,
  output REGFILE_WRITE,
  output RAM_WRITE,
  output [3:0] MAR_WRITE,
  output IO_WRITE,
  output KEYBOARD_WRITE,
  output NIBLE_HIGH_WRITE,
  output NIBLE_LOW_WRITE,
  output PC_ENABLE,
  output PC_OUT_DISABLE,
  output JUMP_ENABLE,
  output RMA_RESET,
  output AMA_RESET,
  output STEP_RESET
);

  wire and_1_out, and_2_out, and_3_out, and_4_out, and_5_out, and_6_out, and_7_out, and_8_out, and_9_out,
       and_10_out, and_11_out, and_12_out, and_13_out, and_14_out, and_15_out, and_16_out, and_20_out,
       and_21_out, and_22_out, and_23_out, and_25_out, and_26_out, and_27_out, and_28_out, and_29_out,
       and_31_out, and_32_out, and_33_out, and_34_out, and_35_out, and_36_out, and_37_out, and_38_out,
       and_39_out, and_40_out, and_41_out, and_42_out, and_43_out, and_44_out, and_45_out, and_46_out,
       and_51_out, and_52_out, and_53_out, and_54_out, and_55_out, and_56_out, and_57_out, and_58_out,
       and_59_out, and_60_out, and_61_out, and_62_out, and_63_out, and_64_out, and_65_out, and_66_out,
       and_67_out, and_68_out, and_69_out, and_70_out, and_71_out, and_72_out, and_73_out, and_74_out,
       and_75_out, and_76_out, and_77_out, and_78_out, and_79_out, and_80_out, and_81_out, and_82_out,
       and_83_out, and_84_out, and_85_out, and_86_out, and_87_out, and_88_out, and_89_out, and_90_out,
       not_1_out, not_2_out, not_3_out, not_4_out, not_5_out, not_6_out, not_7_out, not_8_out;

  not not_1 (not_1_out, INSTRUCTION[3]);
  not not_2 (not_2_out, INSTRUCTION[2]);
  not not_3 (not_3_out, INSTRUCTION[1]);
  not not_4 (not_4_out, INSTRUCTION[0]);
  not not_5 (not_5_out, STEP[3]);
  not not_6 (not_6_out, STEP[2]);
  not not_7 (not_7_out, STEP[1]);
  not not_8 (not_8_out, STEP[0]);
  and and_1 (and_1_out, not_5_out, not_6_out, not_7_out, not_8_out);
  and and_2 (and_2_out, INSTRUCTION[3], not_4_out, not_5_out, not_8_out);
  and and_3 (and_3_out, INSTRUCTION[2], not_4_out, not_5_out, not_8_out);
  and and_4 (and_4_out, INSTRUCTION[2], not_3_out, not_4_out, not_6_out, not_8_out);
  and and_5 (and_5_out, INSTRUCTION[0], not_5_out, not_6_out, not_8_out);
  and and_6 (and_6_out, not_1_out, INSTRUCTION[0], not_5_out, not_7_out, not_8_out);
  and and_7 (and_7_out, INSTRUCTION[1], not_5_out, not_6_out, not_8_out);
  and and_8 (and_8_out, INSTRUCTION[1], INSTRUCTION[0], not_5_out, not_8_out);
  and and_9 (and_9_out, INSTRUCTION[1], INSTRUCTION[0], not_6_out, not_8_out);
  and and_10 (and_10_out, not_2_out, INSTRUCTION[1], INSTRUCTION[0], not_7_out, not_8_out);
  and and_11 (and_11_out, INSTRUCTION[2], not_4_out, not_6_out, not_7_out, not_8_out);
  and and_12 (and_12_out, not_1_out, not_2_out, INSTRUCTION[1], not_4_out, not_5_out, STEP[2], not_7_out, not_8_out);
  and and_13 (and_13_out, not_1_out, INSTRUCTION[2], not_3_out, not_4_out, STEP[3], STEP[2], not_7_out, not_8_out);
  and and_14 (and_14_out, INSTRUCTION[2], INSTRUCTION[1], not_4_out, STEP[3], not_6_out, not_7_out, STEP[0]);
  and and_15 (and_15_out, INSTRUCTION[1], INSTRUCTION[0], STEP[3], STEP[2], not_7_out, not_8_out);
  and and_16 (and_16_out, INSTRUCTION[2], not_3_out, not_4_out, STEP[3], STEP[2], not_7_out, not_8_out);
  and and_17 (IO_READ, INSTRUCTION[3], not_4_out, STEP[3], not_6_out, not_7_out, not_8_out);
  and and_18 (KEYBOARD_READ, INSTRUCTION[3], INSTRUCTION[0], not_5_out, STEP[2], not_7_out, not_8_out);
  and and_19 (INSTRUCTION_REG_WRITE, not_5_out, not_6_out, not_7_out, not_8_out);
  and and_20 (and_20_out, not_3_out, INSTRUCTION[0], not_5_out, not_6_out, STEP[1], not_8_out);
  and and_21 (and_21_out, not_2_out, INSTRUCTION[1], not_4_out, not_5_out, not_6_out, STEP[1], not_8_out);
  and and_22 (and_22_out, INSTRUCTION[2], not_3_out, not_5_out, not_6_out, STEP[1], not_8_out);
  and and_23 (and_23_out, not_2_out, INSTRUCTION[1], INSTRUCTION[0], STEP[3], not_6_out, STEP[1], not_8_out);
  and and_24 (AMA_WRITE, not_1_out, not_2_out, not_3_out, INSTRUCTION[0], not_5_out, STEP[2], not_7_out, not_8_out);
  and and_25 (and_25_out, not_2_out, INSTRUCTION[1], not_4_out, not_5_out, STEP[2], not_7_out, not_8_out);
  and and_26 (and_26_out, INSTRUCTION[2], not_3_out, INSTRUCTION[0], not_5_out, STEP[2], not_7_out, not_8_out);
  and and_27 (and_27_out, INSTRUCTION[3], INSTRUCTION[0], not_5_out, STEP[2], not_7_out, not_8_out);
  and and_28 (and_28_out, not_1_out, not_2_out, not_3_out, INSTRUCTION[0], not_5_out, STEP[2], not_7_out, STEP[0]);
  and and_29 (and_29_out, not_2_out, INSTRUCTION[1], INSTRUCTION[0], STEP[3], STEP[2], not_7_out, not_8_out);
  and and_30 (RAM_WRITE, INSTRUCTION[2], not_3_out, not_4_out, STEP[3], STEP[2], not_7_out, not_8_out);
  and and_31 (and_31_out, not_2_out, INSTRUCTION[1], INSTRUCTION[0], not_5_out, not_6_out, STEP[1], not_8_out);
  and and_32 (and_32_out, INSTRUCTION[2], INSTRUCTION[1], not_4_out, not_5_out, not_6_out, STEP[1], not_8_out);
  and and_33 (and_33_out, INSTRUCTION[2], not_3_out, not_4_out, not_5_out, STEP[2], not_7_out, not_8_out);
  and and_34 (and_34_out, INSTRUCTION[2], INSTRUCTION[1], INSTRUCTION[0], not_5_out, STEP[2], not_7_out, not_8_out);
  and and_35 (and_35_out, not_2_out, INSTRUCTION[1], INSTRUCTION[0], not_5_out, STEP[2], not_7_out, not_8_out);
  and and_36 (and_36_out, INSTRUCTION[2], INSTRUCTION[1], not_4_out, not_5_out, STEP[2], not_7_out, not_8_out);
  and and_37 (and_37_out, INSTRUCTION[2], not_3_out, not_4_out, not_5_out, STEP[2], STEP[1], not_8_out);
  and and_38 (and_38_out, INSTRUCTION[2], INSTRUCTION[1], INSTRUCTION[0], not_5_out, STEP[2], STEP[1], not_8_out);
  and and_39 (and_39_out, not_2_out, INSTRUCTION[1], INSTRUCTION[0], not_5_out, STEP[2], STEP[1], not_8_out);
  and and_40 (and_40_out, INSTRUCTION[2], INSTRUCTION[1], not_4_out, not_5_out, STEP[2], STEP[1], not_8_out);
  and and_41 (and_41_out, INSTRUCTION[2], not_3_out, not_4_out, STEP[3], not_6_out, not_7_out, not_8_out);
  and and_42 (and_42_out, INSTRUCTION[2], INSTRUCTION[1], INSTRUCTION[0], STEP[3], not_6_out, not_7_out, not_8_out);
  and and_43 (and_43_out, not_2_out, INSTRUCTION[1], INSTRUCTION[0], STEP[3], not_6_out, not_7_out, not_8_out);
  and and_44 (and_44_out, INSTRUCTION[2], INSTRUCTION[1], not_4_out, STEP[3], not_6_out, not_7_out, not_8_out);
  and and_45 (and_45_out, INSTRUCTION[2], not_3_out, not_4_out, STEP[3], not_6_out, STEP[1], not_8_out);
  and and_46 (and_46_out, INSTRUCTION[2], INSTRUCTION[1], INSTRUCTION[0], STEP[3], not_6_out, STEP[1], not_8_out);
  and and_47 (IO_WRITE, INSTRUCTION[3], not_4_out, not_5_out, not_6_out, STEP[1], not_8_out);
  and and_48 (KEYBOARD_WRITE, INSTRUCTION[3], INSTRUCTION[0], not_5_out, STEP[2], not_7_out, STEP[0]);
  and and_49 (NIBLE_HIGH_WRITE, INSTRUCTION[3], not_4_out, not_5_out, STEP[2], not_7_out, not_8_out);
  and and_50 (NIBLE_LOW_WRITE, INSTRUCTION[3], not_4_out, not_5_out, STEP[2], STEP[1], not_8_out);
  and and_51 (and_51_out, not_5_out, not_6_out, not_7_out, STEP[0]);
  and and_52 (and_52_out, INSTRUCTION[3], not_4_out, not_5_out, STEP[0]);
  and and_53 (and_53_out, INSTRUCTION[2], not_4_out, not_5_out, STEP[0]);
  and and_54 (and_54_out, INSTRUCTION[2], not_3_out, not_4_out, not_6_out, STEP[0]);
  and and_55 (and_55_out, INSTRUCTION[0], not_5_out, not_6_out, STEP[0]);
  and and_56 (and_56_out, INSTRUCTION[2], not_5_out, not_7_out, STEP[0]);
  and and_57 (and_57_out, not_1_out, not_2_out, not_3_out, INSTRUCTION[0], not_5_out, STEP[2], STEP[1], not_8_out);
  and and_58 (and_58_out, INSTRUCTION[1], not_5_out, not_6_out, STEP[0]);
  and and_59 (and_59_out, INSTRUCTION[1], INSTRUCTION[0], not_5_out, STEP[0]);
  and and_60 (and_60_out, INSTRUCTION[1], INSTRUCTION[0], not_6_out, STEP[0]);
  and and_61 (and_61_out, INSTRUCTION[2], INSTRUCTION[1], not_4_out, STEP[3], not_6_out, not_7_out, STEP[0]);
  and and_62 (and_62_out, INSTRUCTION[1], INSTRUCTION[0], STEP[3], STEP[2], not_7_out, not_8_out);
  and and_63 (and_63_out, INSTRUCTION[2], not_3_out, not_4_out, STEP[3], STEP[2], not_7_out, not_8_out);
  and and_64 (and_64_out, INSTRUCTION[2], INSTRUCTION[1], not_4_out, STEP[3], not_6_out, not_7_out, STEP[0]);
  and and_65 (and_65_out, INSTRUCTION[2], INSTRUCTION[1], INSTRUCTION[0], STEP[3], STEP[2], not_7_out, not_8_out);
  and and_66 (and_66_out, not_1_out, not_2_out, INSTRUCTION[1], not_4_out, not_5_out, STEP[2], not_7_out, STEP[0]);
  and and_67 (and_67_out, INSTRUCTION[3], not_4_out, STEP[3], not_6_out, not_7_out, STEP[0]);
  and and_68 (and_68_out, INSTRUCTION[2], INSTRUCTION[1], not_4_out, STEP[3], not_6_out, STEP[1], not_8_out);
  and and_69 (and_69_out, INSTRUCTION[2], not_3_out, not_4_out, STEP[3], STEP[2], not_7_out, STEP[0]);
  and and_70 (and_70_out, INSTRUCTION[2], not_3_out, INSTRUCTION[0], not_5_out, STEP[2], STEP[1], not_8_out);
  and and_71 (and_71_out, INSTRUCTION[3], INSTRUCTION[0], not_5_out, STEP[2], STEP[1], not_8_out);
  and and_72 (and_72_out, not_1_out, not_2_out, not_3_out, INSTRUCTION[0], not_5_out, STEP[2], STEP[1], STEP[0]);
  and and_73 (and_73_out, INSTRUCTION[1], INSTRUCTION[0], STEP[3], STEP[2], not_7_out, STEP[0]);
  and and_74 (and_74_out, not_1_out, not_2_out, INSTRUCTION[1], not_4_out, not_5_out, STEP[2], not_7_out, STEP[0]);
  and and_75 (and_75_out, INSTRUCTION[3], not_4_out, STEP[3], not_6_out, not_7_out, STEP[0]);
  and and_76 (and_76_out, INSTRUCTION[2], INSTRUCTION[1], not_4_out, STEP[3], not_6_out, STEP[1], not_8_out);
  and and_77 (and_77_out, INSTRUCTION[2], not_3_out, not_4_out, STEP[3], STEP[2], not_7_out, STEP[0]);
  and and_78 (and_78_out, INSTRUCTION[2], not_3_out, INSTRUCTION[0], not_5_out, STEP[2], STEP[1], not_8_out);
  and and_79 (and_79_out, INSTRUCTION[3], INSTRUCTION[0], not_5_out, STEP[2], STEP[1], not_8_out);
  and and_80 (and_80_out, not_1_out, not_2_out, not_3_out, INSTRUCTION[0], not_5_out, STEP[2], STEP[1], STEP[0]);
  and and_81 (and_81_out, INSTRUCTION[1], INSTRUCTION[0], STEP[3], STEP[2], not_7_out, STEP[0]);
  and and_82 (and_82_out, not_1_out, not_2_out, not_3_out, not_4_out, not_5_out, not_6_out, STEP[1], not_8_out);
  and and_83 (and_83_out, not_2_out, INSTRUCTION[1], not_4_out, not_5_out, STEP[2], not_7_out, STEP[0]);
  and and_84 (and_84_out, INSTRUCTION[2], not_3_out, INSTRUCTION[0], not_5_out, STEP[2], STEP[1], not_8_out);
  and and_85 (and_85_out, INSTRUCTION[3], INSTRUCTION[0], not_5_out, STEP[2], STEP[1], not_8_out);
  and and_86 (and_86_out, not_1_out, not_2_out, not_3_out, INSTRUCTION[0], not_5_out, STEP[2], STEP[1], STEP[0]);
  and and_87 (and_87_out, INSTRUCTION[3], not_4_out, STEP[3], not_6_out, not_7_out, STEP[0]);
  and and_88 (and_88_out, INSTRUCTION[2], INSTRUCTION[1], not_4_out, STEP[3], not_6_out, STEP[1], not_8_out);
  and and_89 (and_89_out, INSTRUCTION[1], INSTRUCTION[0], STEP[3], STEP[2], not_7_out, STEP[0]);
  and and_90 (and_90_out, INSTRUCTION[2], not_3_out, not_4_out, STEP[3], STEP[2], not_7_out, STEP[0]);
  or or_1 (RAM_READ, and_1_out, and_2_out, and_3_out, and_4_out, and_5_out, and_6_out, and_7_out, and_8_out, and_9_out, and_10_out, and_11_out);
  or or_2 (REGFILE_READ, and_12_out, and_13_out);
  or or_3 (MAR_READ, and_14_out, and_15_out, and_16_out);
  or or_4 (RMA_WRITE, and_20_out, and_21_out, and_22_out, and_23_out);
  or or_5 (REGFILE_WRITE, and_25_out, and_26_out, and_27_out, and_28_out, and_29_out);
  or or_6 (MAR_WRITE[3], and_31_out, and_32_out, and_33_out, and_34_out);
  or or_7 (MAR_WRITE[2], and_35_out, and_36_out, and_37_out, and_38_out);
  or or_8 (MAR_WRITE[1], and_39_out, and_40_out, and_41_out, and_42_out);
  or or_9 (MAR_WRITE[0], and_43_out, and_44_out, and_45_out, and_46_out);
  or or_10 (PC_ENABLE, and_51_out, and_52_out, and_53_out, and_54_out, and_55_out, and_56_out, and_57_out, and_58_out, and_59_out, and_60_out);
  or or_11 (PC_OUT_DISABLE, and_61_out, and_62_out, and_63_out);
  or or_12 (JUMP_ENABLE, and_64_out, and_65_out);
  or or_13 (RMA_RESET, and_66_out, and_67_out, and_68_out, and_69_out, and_70_out, and_71_out, and_72_out, and_73_out);
  or or_14 (AMA_RESET, and_74_out, and_75_out, and_76_out, and_77_out, and_78_out, and_79_out, and_80_out, and_81_out);
  or or_15 (STEP_RESET, and_82_out, and_83_out, and_84_out, and_85_out, and_86_out, and_87_out, and_88_out, and_89_out, and_90_out);
endmodule
